# Fritzing sketch ArtemisAtpSpeechControledLevel (saved by Fritzing 0.9.3b)
circuit board: 7.50712cm x 4.34621cm
breadboards: 1

parts:
  R4 = Resistor [tolerance=±5% resistance=220 package=THT]
  R3 = Resistor [tolerance=±5% resistance=220 package=THT]
  R2 = Resistor [tolerance=±5% resistance=220 package=THT]
  R1 = Resistor [tolerance=±5% resistance=220 package=THT]
  LED1 = LED - 5mm [color="Red (633nm)" package="5 mm [THT]"]
  LED2 = LED - 5mm [color="Red (633nm)" package="5 mm [THT]"]
  LED3 = LED - 5mm [color="Orange (620nm)" package="5 mm [THT]"]
  LED4 = LED - 5mm [color="Orange (620nm)" package="5 mm [THT]"]
  SparkFun_RedBoard_Artemis_ATP1 = SparkFun RedBoard Artemis ATP

nets:
  N1: R4.Pin_0, R3.Pin_0, R2.Pin_0, R1.Pin_0, SparkFun_RedBoard_Artemis_ATP1.GND
  N2: R4.Pin_1, LED4.cathode
  N3: R3.Pin_1, LED3.cathode
  N4: R2.Pin_1, LED2.cathode
  N5: R1.Pin_1, LED1.cathode
  N6: LED1.anode, SparkFun_RedBoard_Artemis_ATP1.D14
  N7: LED2.anode, SparkFun_RedBoard_Artemis_ATP1.D8
  N8: LED3.anode, SparkFun_RedBoard_Artemis_ATP1.D10
  N9: LED4.anode, SparkFun_RedBoard_Artemis_ATP1.D9

custom parts:
  SparkFun RedBoard Artemis ATP: The RedBoard Artemis ATP is affectionately called 'All the Pins!' at SparkFun. The Artemis module has 48 GPIO and this board breaks out absolutely every one of them in a familiar Mega like form factor. What's with the silkscreen labels? They're all over the place. We decided to label the pins as they are assigned on the Apollo3 IC itself. This makes finding the pin with the function you desire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
